// Digital circuit NonOverlappingClock_BAD.dig as structural Verilog
module NonOverlappingClock_BAD (
  input  clk,
  output out_2,
  output out_3
);

  wire nor_1_out, nor_2_out, not_1_out, not_2_out, not_3_out;

  not not_1 (not_1_out, clk);
  nor nor_1 (nor_1_out, not_1_out, out_3);
  nor nor_2 (nor_2_out, out_2, clk);
  not not_2 (not_2_out, nor_1_out);
  not not_3 (not_3_out, nor_2_out);
  not not_4 (out_2, not_2_out);
  not not_5 (out_3, not_3_out);

  // Notes on the sheet:
  //   This doesn't work. There is supposed to be "dead time"
  //   between the output transitions.
endmodule
